# Fritzing sketch 配線図 (saved by Fritzing 0.9.9b)
breadboards: 1

parts:
  X1 = USB Connectors [package=usb-microb]
  PIC16F1459 = PICAXE-20M [package=THT]
  C1 = Ceramic Capacitor [capacitance=0.1nF voltage=35V package="100 mil [THT, multilayer]"]
  C2 = Ceramic Capacitor [capacitance=0.1nF voltage=35V package="100 mil [THT, multilayer]"]
  LED_Connect = LED - 5mm [color="Blue (525nm)" current=0.030 package="5 mm [THT]"]
  LED_Scanning = LED - 5mm [color="Yellow (595nm)" current=0.030 package="5 mm [THT]"]
  LED_OK = LED - 5mm [color="Green (570nm)" current=0.030 package="5 mm [THT]"]
  LED_NG = LED - 5mm [color="Red (633nm)" current=0.030 package="5 mm [THT]"]
  R1 = Resistor [tolerance=±5% power=0.25 resistance=220 package=THT]
  R2 = Resistor [tolerance=±5% power=0.25 resistance=220 package=THT]
  R3 = Resistor [tolerance=±5% power=0.25 resistance=220 package=THT]
  R4 = Resistor [tolerance=±5% power=0.25 resistance=220 package=THT]
  MQ-3 = MQ-3 breakout

nets:
  N1: X1.D+, PIC16F1459.Serial_Out
  N2: X1.D-, PIC16F1459.Out_0_/_Infraout
  GND: X1.GND, PIC16F1459.0V, C1.1, C2.1, LED_Connect.cathode, LED_Scanning.cathode, LED_OK.cathode, LED_NG.cathode, MQ-3.GND
  N3: X1.VBUS, PIC16F1459.+V, C1.0, MQ-3.VCC
  N4: PIC16F1459.Serial_In, MQ-3.DO
  N5: PIC16F1459.In_7_/_ADC_7, MQ-3.AO
  N6: PIC16F1459.In_5, R1.Pin_1
  N7: PIC16F1459.In_4, R2.Pin_1
  N8: PIC16F1459.In_3_/_ADC_3, R3.Pin_1
  N9: PIC16F1459.In_2_/_ADC_2, R4.Pin_1
  N10: PIC16F1459.Out_1, C2.0
  N11: LED_Connect.anode, R1.Pin_0
  N12: LED_Scanning.anode, R2.Pin_0
  N13: LED_OK.anode, R3.Pin_0
  N14: LED_NG.anode, R4.Pin_0

custom parts:
  MQ-3 breakout: Alcohol sensor is capable of detecting alcohol (ethanol) particles on itself and gives the information in digital form back to us to manipulate with it. SKU:101251 • Voltage: 5V DC • Power: max 750mW • Measurement range: 0.04-4mg/L
